# Fritzing sketch gun (saved by Fritzing 0.9.1b)
circuit board: 1.27cm x 2.54cm
breadboards: 1

parts:
  R1 = Resistor [tolerance=±5% resistance=220 package="1206 [SMD]"]
  S1 = SWITCH-MOMENTARY-2 [package=tactile-switch-1101ne]
  U1 = ATTINY45 [package=so]
  J1 = double row female pin header, 6 pins [form="♀ (female)"]
  J2 = double row female pin header, 6 pins [form="♀ (female)"]

nets:
  N1: R1.Pin_0, U1.PB3(ADC3), J2.pin2
  N2: R1.Pin_1, J2.pin1
  N3: S1.1, U1.PB5(NRES)
  GND: S1.2, U1.GND, J1.pin3, J1.pin4, J2.pin3, J2.pin4
  N4: U1.PB4(ADC2), J1.pin5
  N5: U1.PB0(MOSI), J1.pin1
  N6: U1.PB1(MISO), J1.pin2
  N7: U1.PB2(SCK_ADC1), J2.pin5
  5V: U1.VCC, J1.pin6, J2.pin6
