# Fritzing sketch pcb-pi (saved by Fritzing 0.9.2b)
circuit board: 6.52902cm x 5.61683cm
breadboards: 1

parts:
  U1 = mystery part, 40 pins [chip_label=?]
  +bat- = mystery part, 4 pins [chip_label=?]
  Pro_Mini_3V3 = mystery part, 24 pins [chip_label="pro mini"]
  J5 = female pin header, 2 pins [form="♀ (female)"]
  2 = mystery part, 4 pins [chip_label=?]
  3 = mystery part, 4 pins [chip_label=?]
  A5 = mystery part, 4 pins [chip_label=?]
  A6 = mystery part, 4 pins [chip_label=?]
  A7 = mystery part, 4 pins [chip_label=?]
  13 = mystery part, 4 pins [chip_label=?]
  A4 = mystery part, 4 pins [chip_label=?]
  A6_A7 = female pin header, 2 pins [form="♀ (female)"]
  J7 = female pin header, 2 pins [form="♀ (female)"]
  U13 = mystery part, 3 pins [chip_label=?]
  U14 = mystery part, 3 pins [chip_label=?]
  U15 = mystery part, 3 pins [chip_label=?]
  U16 = mystery part, 3 pins [chip_label=?]
  U17 = mystery part, 3 pins [chip_label=?]
  U18 = mystery part, 3 pins [chip_label=?]
  U19 = mystery part, 3 pins [chip_label=?]
  U20 = mystery part, 3 pins [chip_label=?]
  U21 = mystery part, 3 pins [chip_label=?]
  U22 = mystery part, 3 pins [chip_label=?]
  U23 = mystery part, 3 pins [chip_label=?]
  U24 = mystery part, 3 pins [chip_label=?]
  power_on_→ = double row female pin header, 6 pins [form="♀ (female)"]
  A---1 = female pin header, 2 pins [form="♀ (female)"]
  B---1 = female pin header, 2 pins [form="♀ (female)"]
  1000µF = Electrolytic Capacitor [capacitance=1µF package="200 mil [THT, electrolytic]"]
  47kΩ = Resistor [tolerance=±5% resistance=220 package="1206 [SMD]"]
  47nF = Ceramic Capacitor [capacitance=100nF package="1206 [SMD, multilayer]"]
  47kΩ_2 = Resistor [tolerance=±5% resistance=220 package="1206 [SMD]"]
  R1 = Resistor [tolerance=±5% resistance=220 package="1206 [SMD]"]
  R2 = Resistor [tolerance=±5% resistance=220 package="1206 [SMD]"]

nets:
  N1: U1.pin2, J5.pin2, A4.pin3, R2.Pin_1
  N2: U1.pin3, J5.pin1, A5.pin3, R1.Pin_1
  N3: U1.pin9, R1.Pin_0, R2.Pin_0
  N4: U1.pin20, +bat-.pin1, +bat-.pin4, Pro_Mini_3V3.pin4, Pro_Mini_3V3.pin23, 2.pin1, 3.pin1, A5.pin1, A6.pin1, A7.pin1, 13.pin1, A4.pin1, U13.pin1, U14.pin1, U15.pin1, U16.pin1, U17.pin1, U18.pin1, U19.pin1, U20.pin1, U21.pin1, U22.pin1, U23.pin1, U24.pin1, 1000µF.-, 47kΩ.Pin_1, 47nF.1
  N5: U1.pin39, U1.pin40, Pro_Mini_3V3.pin24, A---1.pin1, 1000µF.+
  N6: +bat-.pin2, +bat-.pin3, power_on_→.pin2, power_on_→.pin3, power_on_→.pin4, power_on_→.pin5
  N7: Pro_Mini_3V3.pin5, 2.pin3
  N8: Pro_Mini_3V3.pin6, 3.pin3
  N9: Pro_Mini_3V3.pin7, U13.pin3
  N10: Pro_Mini_3V3.pin8, U17.pin3
  N11: Pro_Mini_3V3.pin9, U16.pin3
  N12: Pro_Mini_3V3.pin10, U14.pin3
  N13: Pro_Mini_3V3.pin11, U15.pin3
  N14: Pro_Mini_3V3.pin12, U18.pin3
  N15: Pro_Mini_3V3.pin13, U22.pin3
  N16: Pro_Mini_3V3.pin14, U24.pin3
  N17: Pro_Mini_3V3.pin15, U23.pin3
  N18: Pro_Mini_3V3.pin16, 13.pin3
  N19: Pro_Mini_3V3.pin17, U21.pin3
  N20: Pro_Mini_3V3.pin18, U19.pin3
  N21: Pro_Mini_3V3.pin19, U20.pin3
  N22: Pro_Mini_3V3.pin20, 47kΩ.Pin_0, 47nF.0, 47kΩ_2.Pin_1
  N23: Pro_Mini_3V3.pin21, 2.pin4, 3.pin4, A5.pin4, A6.pin4, A7.pin4, 13.pin4, A4.pin4
  N24: 2.pin2, 3.pin2, A5.pin2, A6.pin2, A7.pin2, 13.pin2, A4.pin2, U13.pin2, U14.pin2, U15.pin2, U16.pin2, U17.pin2, U18.pin2, U19.pin2, U20.pin2, U21.pin2, U22.pin2, U23.pin2, U24.pin2, A---1.pin2, B---1.pin1
  N25: A6.pin3, A6_A7.pin2, J7.pin2
  N26: A7.pin3, A6_A7.pin1, J7.pin1
  N27: power_on_→.pin1, power_on_→.pin6, B---1.pin2, 47kΩ_2.Pin_0

notes:
  3V3 * RAW GND
