# Fritzing sketch pcb (saved by Fritzing 0.9.1b)
circuit board: 3.83cm x 3.83cm

parts:
  Part1 = Arduino Pro Mini v13 [part_number="Arduino Pro Mini"]
  C1 = Electrolytic Capacitor [capacitance=100µF part_number=1000µF package="200 mil [THT, electrolytic]"]
  FR2 = rounded female pin header, 3 pins [form="♀ (female rounded)"]
  FR3 = female pin header, 3 pins [form="♀ (female)"]
  FL1 = female pin header, 3 pins [form="♀ (female)"]
  FL2 = female pin header, 3 pins [form="♀ (female)"]
  FL3 = female pin header, 3 pins [form="♀ (female)"]
  HL1 = female pin header, 3 pins [form="♀ (female)"]
  HL2 = female pin header, 3 pins [form="♀ (female)"]
  HL3 = female pin header, 3 pins [form="♀ (female)"]
  HR3 = female pin header, 3 pins [form="♀ (female)"]
  HR2 = female pin header, 3 pins [form="♀ (female)"]
  HR1 = female pin header, 3 pins [form="♀ (female)"]
  ping = male pin header, 4 pins [form="♂ (male)"]
  -_+ = female pin header, 2 pins [form="♀ (female)"]
  FR1 = female pin header, 3 pins [form="♀ (female)"]

nets:
  N1: Part1.VCC, ping.pin4
  GND: Part1.GND, C1.-, FR2.pin1, FR3.pin1, FL1.pin1, FL2.pin1, FL3.pin1, HL1.pin1, HL2.pin1, HL3.pin1, HR3.pin1, HR2.pin1, HR1.pin1, ping.pin1, -_+.pin2, FR1.pin1
  5V: Part1.RAW, C1.+, FR2.pin2, FR3.pin2, FL1.pin2, FL2.pin2, FL3.pin2, HL1.pin2, HL2.pin2, HL3.pin2, HR3.pin2, HR2.pin2, HR1.pin2, -_+.pin1, FR1.pin2
  N2: Part1.A3, ping.pin3
  N3: Part1.A2, HR1.pin3
  N4: Part1.A1, HR2.pin3
  N5: Part1.A0, HR3.pin3
  N6: Part1.D13/SCK, ping.pin2
  N7: Part1.D12/MISO, HL3.pin3
  N8: Part1.D11_PWM/MOSI, HL2.pin3
  N9: Part1.D10_PWM/SS, HL1.pin3
  N10: Part1.D9_PWM, FL1.pin3
  N11: Part1.D8, FL2.pin3
  N12: Part1.D7, FL3.pin3
  N13: Part1.D6_PWM, FR3.pin3
  N14: Part1.D5_PWM, FR2.pin3
  N15: Part1.D4, FR1.pin3
