# Fritzing sketch pcb2 (saved by Fritzing 0.9.2b)
circuit board: 3.83cm x 4.02cm

parts:
  1000µF = Electrolytic Capacitor [capacitance=100µF part_number=1000µF package="200 mil [THT, electrolytic]"]
  FR1 = male pin header, 3 pins [form="♂ (male)"]
  FR2 = rounded female pin header, 3 pins [form="♀ (female rounded)"]
  FR3 = female pin header, 3 pins [form="♀ (female)"]
  -_+_s = female pin header, 3 pins [form="♀ (female)"]
  FL2 = female pin header, 3 pins [form="♀ (female)"]
  FL3 = female pin header, 3 pins [form="♀ (female)"]
  s_+_- = female pin header, 3 pins [form="♀ (female)"]
  HL2 = female pin header, 3 pins [form="♀ (female)"]
  HL3 = female pin header, 3 pins [form="♀ (female)"]
  HR3 = female pin header, 3 pins [form="♀ (female)"]
  HR2 = female pin header, 3 pins [form="♀ (female)"]
  +_3_13_- = male pin header, 4 pins [form="♂ (male)"]
  47nF = Ceramic Capacitor [capacitance=100nF package="1206 [SMD, multilayer]"]
  47kΩ = Resistor [tolerance=±5% resistance=47k package="1206 [SMD]"]
  47kΩ_2 = Resistor [tolerance=±5% resistance=47k package="1206 [SMD]"]
  V15 = DC Power [voltage=5]
  power_on = male pin header, 3 pins [form="♂ (male)"]
  Part1 = Arduino Pro Mini v13 [part_number="Arduino Pro Mini"]
  s_+_-_2 = female pin header, 3 pins [form="♀ (female)"]
  -_+_2 = male pin header, 3 pins [form="♂ (male)"]
  +_SDA_SCL_- = male pin header, 4 pins [form="♂ (male)"]
  J6 = male pin header, 7 pins [form="♂ (male)"]
  J4 = male pin header, 8 pins [form="♂ (male)"]  # not connected
  J5 = male pin header, 8 pins [form="♂ (male)"]  # not connected
  --- = male pin header, 4 pins [form="♂ (male)"]
  +Bat- = female pin header, 2 pins [form="♀ (female)"]
  J2 = male pin header, 10 pins [form="♂ (male)"]
  J13 = male pin header, 8 pins [form="♂ (male)"]  # not connected

nets:
  GND: 1000µF.-, FR1.pin1, FR2.pin1, FR3.pin1, -_+_s.pin1, FL2.pin1, FL3.pin1, s_+_-.pin1, HL2.pin1, HL3.pin1, HR3.pin1, HR2.pin1, +_3_13_-.pin1, 47nF.1, 47kΩ_2.Pin_1, V15.V-, power_on.pin3, Part1.GND, s_+_-_2.pin1, -_+_2.pin1, +_SDA_SCL_-.pin1, J6.pin1, ---.pin4, +Bat-.pin2, J2.pin4
  5V: 1000µF.+, FR1.pin2, FR2.pin2, FR3.pin2, -_+_s.pin2, FL2.pin2, FL3.pin2, s_+_-.pin2, HL2.pin2, HL3.pin2, HR3.pin2, HR2.pin2, Part1.RAW, s_+_-_2.pin2, J6.pin7, ---.pin1, J2.pin10
  N1: FR1.pin3, Part1.D4
  N2: FR2.pin3, Part1.D5_PWM
  N3: FR3.pin3, Part1.D6_PWM
  N4: -_+_s.pin3, Part1.D9_PWM
  N5: FL2.pin3, Part1.D8
  N6: FL3.pin3, Part1.D7
  N7: s_+_-.pin3, Part1.D10_PWM/SS
  N8: HL2.pin3, Part1.D11_PWM/MOSI
  N9: HL3.pin3, Part1.D12/MISO
  N10: HR3.pin3, Part1.A0
  N11: HR2.pin3, Part1.A1
  N12: +_3_13_-.pin2, Part1.D13/SCK
  N13: +_3_13_-.pin3, Part1.D3_PWM
  N14: +_3_13_-.pin4, Part1.VCC, -_+_2.pin2, +_SDA_SCL_-.pin4
  N15: 47nF.0, 47kΩ.Pin_0, 47kΩ_2.Pin_0, Part1.A3
  N16: 47kΩ.Pin_1, power_on.pin2, ---.pin2
  N17: power_on.pin1, ---.pin3, +Bat-.pin1
  N18: Part1.A4, +_SDA_SCL_-.pin3
  N19: Part1.A5, +_SDA_SCL_-.pin2
  N20: Part1.A2, s_+_-_2.pin3
  N21: Part1.D2, -_+_2.pin3
