# Fritzing sketch pcb3 (saved by Fritzing 0.9.2b)
circuit board: 3.83cm x 3.83cm

parts:
  1000µF = Electrolytic Capacitor [capacitance=100µF part_number=1000µF package="200 mil [THT, electrolytic]"]
  FR1 = male pin header, 3 pins [form="♂ (male)"]
  FR2 = rounded female pin header, 3 pins [form="♀ (female rounded)"]
  FR3 = female pin header, 3 pins [form="♀ (female)"]
  -_+_s = female pin header, 3 pins [form="♀ (female)"]
  FL2 = female pin header, 3 pins [form="♀ (female)"]
  FL3 = female pin header, 3 pins [form="♀ (female)"]
  s_+_- = female pin header, 3 pins [form="♀ (female)"]
  HL2 = female pin header, 3 pins [form="♀ (female)"]
  HL3 = female pin header, 3 pins [form="♀ (female)"]
  HR3 = female pin header, 3 pins [form="♀ (female)"]
  HR2 = female pin header, 3 pins [form="♀ (female)"]
  47nF = Ceramic Capacitor [capacitance=100nF package="1206 [SMD, multilayer]"]
  47kΩ = Resistor [tolerance=±5% resistance=47k package="1206 [SMD]"]
  47kΩ_2 = Resistor [tolerance=±5% resistance=47k package="1206 [SMD]"]
  Part1 = Arduino Pro Mini v13 [part_number="Arduino Pro Mini"]
  s_+_-_2 = female pin header, 3 pins [form="♀ (female)"]
  2_-_+ = male pin header, 3 pins [form="♂ (male)"]
  +_SDA_SCL_- = male pin header, 4 pins [form="♂ (male)"]
  |_0 = male pin header, 3 pins [form="♂ (male)"]
  --- = female pin header, 2 pins [form="♀ (female)"]
  ---_2 = female pin header, 2 pins [form="♀ (female)"]
  A6_A7 = female pin header, 2 pins [form="♀ (female)"]
  A6_A7_2 = female pin header, 2 pins [form="♀ (female)"]
  +BAT- = double row female pin header, 4 pins [form="♀ (female)"]
  buzzer = Piezo Speaker
  +_3_- = male pin header, 3 pins [form="♂ (male)"]

nets:
  GND: 1000µF.-, FR1.pin1, FR2.pin1, FR3.pin1, -_+_s.pin1, FL2.pin1, FL3.pin1, s_+_-.pin1, HL2.pin1, HL3.pin1, HR3.pin1, HR2.pin1, 47nF.1, 47kΩ_2.Pin_1, Part1.GND, s_+_-_2.pin1, 2_-_+.pin2, +_SDA_SCL_-.pin1, +BAT-.pin1, +BAT-.pin4, buzzer.pin1, +_3_-.pin3
  5V: 1000µF.+, FR1.pin2, FR2.pin2, FR3.pin2, -_+_s.pin2, FL2.pin2, FL3.pin2, s_+_-.pin2, HL2.pin2, HL3.pin2, HR3.pin2, HR2.pin2, 47kΩ.Pin_1, Part1.RAW, s_+_-_2.pin2, |_0.pin1, ---.pin1, ---.pin2, ---_2.pin1, ---_2.pin2
  N1: FR1.pin3, Part1.D4
  N2: FR2.pin3, Part1.D5_PWM
  N3: FR3.pin3, Part1.D6_PWM
  N4: -_+_s.pin3, Part1.D9_PWM
  N5: FL2.pin3, Part1.D8
  N6: FL3.pin3, Part1.D7
  N7: s_+_-.pin3, Part1.D10_PWM/SS
  N8: HL2.pin3, Part1.D11_PWM/MOSI
  N9: HL3.pin3, Part1.D12/MISO
  N10: HR3.pin3, Part1.A0
  N11: HR2.pin3, Part1.A1
  N12: 47nF.0, 47kΩ.Pin_0, 47kΩ_2.Pin_0, Part1.A3
  3.3V: Part1.VCC, 2_-_+.pin3, +_SDA_SCL_-.pin4, +_3_-.pin1
  N13: Part1.A4, +_SDA_SCL_-.pin3
  N14: Part1.A5, +_SDA_SCL_-.pin2
  N15: Part1.A2, s_+_-_2.pin3
  N16: Part1.D13/SCK, buzzer.pin2
  N17: Part1.D3_PWM, +_3_-.pin2
  N18: Part1.D2, 2_-_+.pin1
  N19: |_0.pin2, |_0.pin3, +BAT-.pin2, +BAT-.pin3
  N20: A6_A7.pin1, A6_A7_2.pin2
  N21: A6_A7.pin2, A6_A7_2.pin1
