# Fritzing sketch pcb4 (saved by Fritzing 0.9.2b)
circuit board: 4.95cm x 4.95cm
breadboards: 1

parts:
  U1 = mystery part, 3 pins [chip_label=?]
  U2 = mystery part, 3 pins [chip_label=?]
  U3 = mystery part, 3 pins [chip_label=?]
  U4 = mystery part, 3 pins [chip_label=?]
  U5 = mystery part, 3 pins [chip_label=?]
  U6 = mystery part, 3 pins [chip_label=?]
  U7 = mystery part, 3 pins [chip_label=?]
  U8 = mystery part, 3 pins [chip_label=?]
  U9 = mystery part, 3 pins [chip_label=?]
  U10 = mystery part, 3 pins [chip_label=?]
  U11 = mystery part, 3 pins [chip_label=?]
  U12 = mystery part, 3 pins [chip_label=?]
  47kΩ = Resistor [tolerance=±5% resistance=220 package="1206 [SMD]"]
  47kΩ_2 = Resistor [tolerance=±5% resistance=220 package="1206 [SMD]"]
  47nF = Ceramic Capacitor [capacitance=100nF package="1206 [SMD, multilayer]"]
  power_on_→ = double row female pin header, 6 pins [form="♀ (female)"]
  ---B = female pin header, 2 pins [form="♀ (female)"]
  A--- = female pin header, 2 pins [form="♀ (female)"]
  1000µF = Electrolytic Capacitor [capacitance=1µF package="200 mil [THT, electrolytic]"]
  A6_A7 = female pin header, 2 pins [form="♀ (female)"]
  J2 = female pin header, 2 pins [form="♀ (female)"]
  3 = mystery part, 4 pins [chip_label=?]
  2 = mystery part, 4 pins [chip_label=?]
  A5 = mystery part, 4 pins [chip_label=?]
  A4 = mystery part, 4 pins [chip_label=?]
  13 = mystery part, 4 pins [chip_label=?]
  A6 = mystery part, 4 pins [chip_label=?]
  A7 = mystery part, 4 pins [chip_label=?]
  rx_tx = female pin header, 2 pins [form="♀ (female)"]
  J3 = double row female pin header, 6 pins [form="♀ (female)"]  # not connected
  Pro_Mini_3V3 = mystery part, 24 pins [chip_label="pro mini"]
  J4 = female pin header, 2 pins [form="♀ (female)"]
  +bat- = mystery part, 4 pins [chip_label=?]

nets:
  N1: U1.pin1, U2.pin1, U3.pin1, U4.pin1, U5.pin1, U6.pin1, U7.pin1, U8.pin1, U9.pin1, U10.pin1, U11.pin1, U12.pin1, 1000µF.-, 3.pin1, 2.pin1, A5.pin1, A4.pin1, 13.pin1, A6.pin1, A7.pin1, Pro_Mini_3V3.pin4, Pro_Mini_3V3.pin23, +bat-.pin1, +bat-.pin4
  N2: U1.pin2, U2.pin2, U3.pin2, U4.pin2, U5.pin2, U6.pin2, U7.pin2, U8.pin2, U9.pin2, U10.pin2, U11.pin2, U12.pin2, 47kΩ_2.Pin_1, power_on_→.pin1, power_on_→.pin6, ---B.pin1, ---B.pin2, A---.pin1, A---.pin2, 1000µF.+, 3.pin2, 2.pin2, A5.pin2, A4.pin2, 13.pin2, A6.pin2, A7.pin2, Pro_Mini_3V3.pin24
  N3: U1.pin3, Pro_Mini_3V3.pin19
  N4: U2.pin3, Pro_Mini_3V3.pin18
  N5: U3.pin3, Pro_Mini_3V3.pin17
  N6: U4.pin3, Pro_Mini_3V3.pin15
  N7: U5.pin3, Pro_Mini_3V3.pin14
  N8: U6.pin3, Pro_Mini_3V3.pin13
  N9: U7.pin3, Pro_Mini_3V3.pin12
  N10: U8.pin3, Pro_Mini_3V3.pin7
  N11: U9.pin3, Pro_Mini_3V3.pin10
  N12: U10.pin3, Pro_Mini_3V3.pin11
  N13: U11.pin3, Pro_Mini_3V3.pin9
  N14: U12.pin3, Pro_Mini_3V3.pin8
  N15: 47kΩ.Pin_0, 47kΩ_2.Pin_0, 47nF.0, Pro_Mini_3V3.pin20
  N16: 47kΩ.Pin_1, 47nF.1
  N17: power_on_→.pin2, power_on_→.pin3, power_on_→.pin4, power_on_→.pin5, +bat-.pin2, +bat-.pin3
  N18: A6_A7.pin1, J2.pin1, A7.pin3
  N19: A6_A7.pin2, J2.pin2, A6.pin3
  N20: 3.pin3, Pro_Mini_3V3.pin6
  N21: 3.pin4, 2.pin4, A5.pin4, A4.pin4, 13.pin4, A6.pin4, A7.pin4, Pro_Mini_3V3.pin21
  N22: 2.pin3, Pro_Mini_3V3.pin5
  N23: A5.pin3, J4.pin1
  N24: A4.pin3, J4.pin2
  N25: 13.pin3, Pro_Mini_3V3.pin16
  N26: rx_tx.pin1, Pro_Mini_3V3.pin1
  N27: rx_tx.pin2, Pro_Mini_3V3.pin2

notes:
  3V3 * RAW GND
