# Fritzing sketch pvb2 (saved by Fritzing 0.9.1b)
circuit board: 4.97cm x 4.97cm

parts:
  C1 = Electrolytic Capacitor [capacitance=100µF part_number=1000µF package="200 mil [THT, electrolytic]"]
  FR1 = male pin header, 3 pins [form="♂ (male)"]
  FR2 = rounded female pin header, 3 pins [form="♀ (female rounded)"]
  FR3 = female pin header, 3 pins [form="♀ (female)"]
  FL1 = female pin header, 3 pins [form="♀ (female)"]
  FL2 = female pin header, 3 pins [form="♀ (female)"]
  FL3 = female pin header, 3 pins [form="♀ (female)"]
  HL1 = female pin header, 3 pins [form="♀ (female)"]
  HL2 = female pin header, 3 pins [form="♀ (female)"]
  HL3 = female pin header, 3 pins [form="♀ (female)"]
  HR3 = female pin header, 3 pins [form="♀ (female)"]
  HR2 = female pin header, 3 pins [form="♀ (female)"]
  ping = male pin header, 4 pins [form="♂ (male)"]
  C2 = Ceramic Capacitor [capacitance=100nF package="1206 [SMD, multilayer]"]
  R2 = Resistor [tolerance=±5% resistance=47k package="1206 [SMD]"]
  R1 = Resistor [tolerance=±5% resistance=47k package="1206 [SMD]"]
  V15 = DC Power [voltage=5]
  ON = male pin header, 3 pins [form="♂ (male)"]
  Part1 = Arduino Pro Mini v13 [part_number="Arduino Pro Mini"]
  HR1 = female pin header, 3 pins [form="♀ (female)"]
  sensor = male pin header, 3 pins [form="♂ (male)"]
  I2C = male pin header, 4 pins [form="♂ (male)"]
  J6 = male pin header, 7 pins [form="♂ (male)"]
  J4 = male pin header, 8 pins [form="♂ (male)"]  # not connected
  J5 = male pin header, 8 pins [form="♂ (male)"]  # not connected
  ON1 = male pin header, 4 pins [form="♂ (male)"]
  + = female pin header, 2 pins [form="♀ (female)"]
  J2 = male pin header, 10 pins [form="♂ (male)"]
  J7 = double row smd female pin header, 8 pins [form="♀ (female)"]
  J8 = double row smd female pin header, 6 pins [form="♀ (female)"]
  J9 = double row smd female pin header, 6 pins [form="♀ (female)"]
  R3 = Resistor [tolerance=±5% resistance=220 package="1206 [SMD]"]
  S1 = SWITCH-MOMENTARY-2 [package=tactile-switch-1101ne]
  J10 = male pin header, 3 pins [form="♂ (male)"]
  J13 = male pin header, 8 pins [form="♂ (male)"]  # not connected
  J11 = male pin header, 3 pins [form="♂ (male)"]
  J14 = female pin header, 2 pins [form="♀ (female)"]
  J15 = female pin header, 2 pins [form="♀ (female)"]
  J19 = female pin header, 14 pins [form="♀ (female)"]
  J22 = female pin header, 4 pins [form="♀ (female)"]
  J16 = female pin header, 19 pins [form="♀ (female)"]
  J23 = female pin header, 2 pins [form="♀ (female)"]
  J24 = female pin header, 2 pins [form="♀ (female)"]
  J25 = female pin header, 2 pins [form="♀ (female)"]
  J26 = female pin header, 2 pins [form="♀ (female)"]

nets:
  GND: C1.-, FR1.pin1, FR2.pin1, FR3.pin1, FL1.pin1, FL2.pin1, FL3.pin1, HL1.pin1, HL2.pin1, HL3.pin1, HR3.pin1, HR2.pin1, ping.pin1, C2.1, R1.Pin_1, V15.V-, ON.pin3, Part1.GND, HR1.pin1, sensor.pin1, I2C.pin1, J6.pin1, ON1.pin4, +.pin2, J2.pin4
  5V: C1.+, FR1.pin2, FR2.pin2, FR3.pin2, FL1.pin2, FL2.pin2, FL3.pin2, HL1.pin2, HL2.pin2, HL3.pin2, HR3.pin2, HR2.pin2, Part1.RAW, HR1.pin2, J6.pin7, ON1.pin1, J2.pin10
  N1: FR1.pin3, Part1.D4
  N2: FR2.pin3, Part1.D5_PWM
  N3: FR3.pin3, Part1.D6_PWM
  N4: FL1.pin3, Part1.D9_PWM
  N5: FL2.pin3, Part1.D8
  N6: FL3.pin3, Part1.D7
  N7: HL1.pin3, Part1.D10_PWM/SS
  N8: HL2.pin3, Part1.D11_PWM/MOSI
  N9: HL3.pin3, Part1.D12/MISO
  N10: HR3.pin3, Part1.A0
  N11: HR2.pin3, Part1.A1
  N12: ping.pin2, Part1.D13/SCK
  N13: ping.pin3, Part1.D3_PWM
  N14: ping.pin4, Part1.VCC, sensor.pin2, I2C.pin4
  N15: C2.0, R2.Pin_0, R1.Pin_0, Part1.A3
  N16: R2.Pin_1, ON.pin2, ON1.pin2
  N17: ON.pin1, ON1.pin3, +.pin1
  N18: Part1.A4, I2C.pin3
  N19: Part1.A5, I2C.pin2
  N20: Part1.A2, HR1.pin3
  N21: Part1.D2, sensor.pin3
  N22: J7.pin1, J9.pin1
  N23: J7.pin2, J9.pin2
  N24: J7.pin3, J8.pin5
  N25: J7.pin4, J8.pin6, J9.pin6, J10.pin3
  N26: J7.pin5, S1.1
  N27: J7.pin6, J8.pin2, R3.Pin_0, J11.pin2
  N28: J7.pin7, J9.pin5, J10.pin2
  N29: J7.pin8, J8.pin3, J8.pin4, J9.pin3, J9.pin4, S1.2, J10.pin1, J11.pin1
  N30: J8.pin1, R3.Pin_1, J11.pin3
  N31: J14.pin1, J16.pin16
  N32: J14.pin2, J16.pin18
  N33: J15.pin1, J19.pin2, J19.pin3, J23.pin1, J23.pin2
  N34: J15.pin2, J19.pin1, J19.pin4, J19.pin14, J25.pin1, J25.pin2
  N35: J22.pin1, J16.pin19, J26.pin1, J26.pin2
  N36: J22.pin2, J16.pin2
  N37: J22.pin3, J16.pin3
  N38: J22.pin4, J24.pin1, J24.pin2
